// Digital circuit Design.dig as structural Verilog
module Design (
  input  in_1,
  input  in_2,
  output out_3
);

  wire and_1_out, not_1_out, not_2_out;

  not not_1 (not_1_out, in_1);
  not not_2 (not_2_out, in_2);
  and and_1 (and_1_out, not_1_out, not_2_out);
  not not_3 (out_3, and_1_out);
endmodule
