// Digital circuit Design.dig as structural Verilog
module Design (
  input  x_0,
  input  x_1,
  output z
);

  wire and_1_out, and_2_out, not_1_out, not_2_out;

  not not_1 (not_1_out, x_0);
  not not_2 (not_2_out, x_1);
  and and_1 (and_1_out, not_1_out, not_2_out);
  and and_2 (and_2_out, x_0, x_1);
  or or_1 (z, and_1_out, and_2_out);
endmodule
