// Digital circuit Design.dig as structural Verilog
module Design (
  input  a,
  input  b,
  input  r,
  output S,
  output R_2
);

  wire and_1_out, and_2_out, and_3_out, and_4_out, and_5_out, and_6_out, and_7_out, and_8_out, not_1_out,
       not_2_out, not_3_out;

  not not_1 (not_1_out, r);
  not not_2 (not_2_out, a);
  not not_3 (not_3_out, b);
  and and_1 (and_1_out, not_1_out, not_2_out, b);
  and and_2 (and_2_out, not_1_out, a, not_3_out);
  and and_3 (and_3_out, r, not_2_out, not_3_out);
  and and_4 (and_4_out, r, a, b);
  and and_5 (and_5_out, not_1_out, a, b);
  and and_6 (and_6_out, r, not_2_out, b);
  and and_7 (and_7_out, r, a, not_3_out);
  and and_8 (and_8_out, r, a, b);
  or or_1 (S, and_1_out, and_2_out, and_3_out, and_4_out);
  or or_2 (R_2, and_5_out, and_6_out, and_7_out, and_8_out);
endmodule
