// Digital circuit Design.dig as structural Verilog
module Design (
  input  a,
  input  b,
  input  r,
  output S,
  output R_2
);

  wire not_1_out, not_2_out, not_3_out, or_1_out, or_2_out, or_3_out, or_4_out, or_5_out, or_6_out, or_7_out,
       or_8_out;

  not not_1 (not_1_out, r);
  not not_2 (not_2_out, a);
  not not_3 (not_3_out, b);
  or or_1 (or_1_out, r, a, b);
  or or_2 (or_2_out, r, not_2_out, not_3_out);
  or or_3 (or_3_out, not_1_out, a, not_3_out);
  or or_4 (or_4_out, not_1_out, not_2_out, b);
  or or_5 (or_5_out, r, a, b);
  or or_6 (or_6_out, r, a, not_3_out);
  or or_7 (or_7_out, r, not_2_out, b);
  or or_8 (or_8_out, not_1_out, a, b);
  and and_1 (S, or_1_out, or_2_out, or_3_out, or_4_out);
  and and_2 (R_2, or_5_out, or_6_out, or_7_out, or_8_out);
endmodule
