// Digital circuit Design.dig as structural Verilog
module Design (
  input  x_0,
  input  x_1,
  input  x_2,
  input  x_3,
  input  x_4,
  input  x_5,
  input  x_6,
  input  x_7,
  input  x_8,
  input  x_9,
  input  x_10,
  input  x_11,
  input  x_12,
  input  x_13,
  input  x_14,
  input  x_15,
  input  x_0_2,
  input  x_1_2,
  input  x_2_2,
  input  x_3_2,
  input  x_4_2,
  input  x_5_2,
  input  x_6_2,
  input  x_7_2,
  input  x_8_2,
  input  x_9_2,
  input  x_10_2,
  input  x_11_2,
  input  x_12_2,
  input  x_13_2,
  input  x_14_2,
  input  x_15_2,
  output z,
  output out_34
);

  wire or_1_out, or_2_out;

  or or_1 (or_1_out, x_0, x_1, x_2, x_3, x_4, x_5, x_6, x_7);
  or or_2 (or_2_out, x_8, x_9, x_10, x_11, x_12, x_13, x_14, x_15);
  or or_3 (z, or_1_out, or_2_out);
  or or_4 (out_34, x_0_2, x_1_2, x_2_2, x_3_2, x_4_2, x_5_2, x_6_2, x_7_2, x_8_2, x_9_2, x_10_2, x_11_2, x_12_2, x_13_2, x_14_2, x_15_2);

  // Notes on the sheet:
  //   =
endmodule
