// Digital circuit Design.dig as structural Verilog
module Design (
  input  x,
  input  y,
  input  x_2,
  input  y_2,
  input  y_3,
  input  x_3,
  input  y_4,
  input  x_4,
  input  x_5,
  input  y_5,
  input  z_5,
  input  x_6,
  input  y_6,
  input  z_6,
  input  x_7,
  input  y_7,
  input  z_7,
  input  x_8,
  input  y_8,
  input  z_8,
  input  x_9,
  input  y_9,
  input  z_9,
  input  x_10,
  input  y_10,
  input  z_10,
  input  x_11,
  input  y_11,
  input  z_11,
  input  x_12,
  input  y_12,
  input  z_12,
  input  x_14,
  input  x_15,
  input  x_17,
  input  _0,
  input  x_19,
  input  _1,
  input  x_21,
  input  _1_2,
  input  x_22,
  input  _0_2,
  input  x_24,
  input  x_25,
  input  x_26,
  input  x_27,
  input  y_13,
  input  x_29,
  input  y_14,
  input  in_74,
  input  in_75,
  input  in_76,
  input  in_77,
  input  in_80,
  input  in_81,
  input  in_82,
  input  in_83,
  input  in_85,
  input  in_86,
  input  in_87,
  input  in_89,
  input  in_90,
  input  in_91,
  input  in_93,
  input  in_94,
  input  in_95,
  input  in_97,
  input  in_98,
  input  in_99,
  output z,
  output z_2,
  output z_3,
  output z_4,
  output w,
  output w_2,
  output w_3,
  output w_4,
  output w_5,
  output w_6,
  output w_7,
  output w_8,
  output x_13,
  output x_16,
  output x_18,
  output x_20,
  output _1_3,
  output _0_3,
  output x_23,
  output _1_4,
  output _0_4,
  output x_28,
  output x_30,
  output out_73,
  output out_78,
  output out_79,
  output out_84,
  output out_88,
  output out_92,
  output out_96,
  output out_100
);

  wire and_1_out, and_2_out, and_3_out, and_4_out, and_5_out, and_6_out, and_7_out, and_8_out, and_9_out,
       and_21_out, and_24_out, and_25_out, not_1_out, not_2_out, not_3_out, not_4_out, not_5_out, not_6_out,
       not_8_out, not_11_out, not_12_out, not_13_out, not_14_out, not_15_out, not_16_out, or_1_out, or_2_out,
       or_3_out, or_4_out, or_5_out, or_6_out, or_7_out, or_8_out, or_9_out, or_21_out, or_24_out, or_25_out;

  not not_1 (not_1_out, in_85);
  not not_2 (not_2_out, in_89);
  and and_1 (and_1_out, x_9, y_9);
  and and_2 (and_2_out, x_9, z_9);
  or or_1 (or_1_out, x_10, y_10);
  or or_2 (or_2_out, x_10, z_10);
  and and_3 (and_3_out, x_27, y_13);
  and and_4 (and_4_out, x_27, not_3_out);
  not not_3 (not_3_out, y_13);
  or or_3 (or_3_out, x_29, y_14);
  or or_4 (or_4_out, x_29, not_4_out);
  not not_4 (not_4_out, y_14);
  and and_5 (and_5_out, in_85, in_86);
  and and_6 (and_6_out, not_1_out, in_87);
  and and_7 (and_7_out, in_86, in_87);
  or or_5 (or_5_out, in_89, in_90);
  or or_6 (or_6_out, not_2_out, in_91);
  or or_7 (or_7_out, in_90, in_91);
  and and_8 (and_8_out, x_5, y_5);
  or or_8 (or_8_out, x_6, y_6);
  not not_5 (not_5_out, x_25);
  not not_6 (not_6_out, x_26);
  or or_9 (or_9_out, in_74, in_75);
  and and_9 (and_9_out, in_80, in_81);
  and and_10 (z, x, y);
  or or_10 (z_2, x_2, y_2);
  and and_11 (w, and_8_out, z_5);
  or or_11 (w_2, or_8_out, z_6);
  or or_12 (w_5, and_1_out, and_2_out);
  and and_12 (w_6, or_1_out, or_2_out);
  and and_13 (x_13, x_14, x_14);
  or or_13 (x_16, x_15, x_15);
  or or_14 (x_18, x_17, _0);
  and and_14 (x_20, x_19, _1);
  or or_15 (_1_3, x_21, _1_2);
  and and_15 (_0_3, x_22, _0_2);
  not not_7 (x_23, not_8_out);
  not not_8 (not_8_out, x_24);
  or or_16 (_1_4, x_25, not_5_out);
  and and_16 (_0_4, x_26, not_6_out);
  or or_17 (x_28, and_3_out, and_4_out);
  and and_17 (x_30, or_3_out, or_4_out);
  not not_9 (out_73, or_9_out);
  not not_10 (out_79, and_9_out);
  or or_18 (out_88, and_5_out, and_6_out, and_7_out);
  and and_18 (out_92, or_5_out, or_6_out, or_7_out);
  and and_19 (z_3, y_3, x_3);
  or or_19 (z_4, y_4, x_4);
  and and_20 (w_3, x_7, y_7, z_7);
  or or_20 (w_4, x_8, y_8, z_8);
  or or_21 (or_21_out, y_11, z_11);
  and and_21 (and_21_out, y_12, z_12);
  not not_11 (not_11_out, in_76);
  not not_12 (not_12_out, in_77);
  not not_13 (not_13_out, in_82);
  not not_14 (not_14_out, in_83);
  and and_22 (w_7, x_11, or_21_out);
  or or_22 (w_8, x_12, and_21_out);
  and and_23 (out_78, not_11_out, not_12_out);
  or or_23 (out_84, not_13_out, not_14_out);
  not not_15 (not_15_out, in_93);
  not not_16 (not_16_out, in_97);
  and and_24 (and_24_out, in_93, in_94);
  and and_25 (and_25_out, not_15_out, in_95);
  or or_24 (or_24_out, in_97, in_98);
  or or_25 (or_25_out, not_16_out, in_99);
  or or_26 (out_96, and_24_out, and_25_out);
  and and_26 (out_100, or_24_out, or_25_out);

  // Notes on the sheet:
  //   _1: default 1
  //   _1_2: default 1
  //   =
  //   E1) commutative
  //   E2) associative
  //   E3) distributive
  //   E4) idempotence
  //   E5) identity
  //   E6) limit
  //   E7) involution
  //   E8) limitation
  //   E9) combination
  //   E10) The De Morgan laws
  //   E11) consent
endmodule
